# Fritzing sketch ON_OFF_DETECTION (saved by Fritzing 0.7.11b)
perfboards: 1

parts:
  U1 = Arduino Mega
  Resistor_10k_Ohm = Resistor [tolerance=±5% resistance=10k package=THT]
  Photoresistor_(LDR) = Photocell (LDR) [package=THT]

nets:
  N1: U1.+5V, Resistor_10k_Ohm.Pin_0
  N2: U1.GND, Photoresistor_(LDR).pin_0
  N3: U1.A0, Resistor_10k_Ohm.Pin_1, Photoresistor_(LDR).pin_1

notes:
  Simple Pull-up circuit
  10K Ohm
  LDR
